// Logisim project alu.circ as structural Verilog: 7 circuits, main circuit main
module main (
  input  [31:0] X,
  input  [31:0] Y,
  input  [3:0] Switch,
  output Signed_Overflow,
  output Equal,
  output [31:0] Result,
  output [31:0] Result_2
);

  wire [31:0] Add_Sub_result, And_Or_result, Div_result, Div_result_2, Mult_result, Mult_result_2, Shift_out,
       Slt_out_4;

  Comparator #(.width(32), .mode("unsigned")) comparator_1 (.a(X), .b(Y), .eq(Equal));  // open: gt, lt
  Shift Shift (.X(X), .Y(Y), .in_3(Switch), .out(Shift_out));
  Add_Subtract Add_Sub (.X(X), .Y(Y), .selector(Switch), .result(Add_Sub_result), .OF(Signed_Overflow));
  AND_OR_OUTER And_Or (.X(X), .Y(Y), .select(Switch), .result(And_Or_result));
  Mult Mult (.X(X), .Y(Y), .result(Mult_result), .result_2(Mult_result_2));
  Div Div (.X(X), .Y(Y), .result(Div_result), .result_2(Div_result_2));
  slt Slt (.X(X), .Y(Y), .select(Switch), .out_4(Slt_out_4));
  Multiplexer #(.select(4), .width(32)) multiplexer_1 (
    .in0(Shift_out), .in1(Shift_out), .in2(Shift_out), .in3(Mult_result), .in4(Div_result),
    .in5(Add_Sub_result), .in6(Add_Sub_result), .in7(Add_Sub_result), .in8(Add_Sub_result),
    .in9(And_Or_result), .in10(And_Or_result), .in11(Slt_out_4), .in12(Slt_out_4), .in13({32{1'b0}}),
    .in14({32{1'b0}}), .in15({32{1'b0}}), .out(Result), .sel(Switch));  // open: en
  Multiplexer #(.select(4), .width(32)) multiplexer_2 (
    .in0({32{1'b0}}), .in1({32{1'b0}}), .in2({32{1'b0}}), .in3(Mult_result_2), .in4(Div_result_2),
    .in5({32{1'b0}}), .in6({32{1'b0}}), .in7({32{1'b0}}), .in8({32{1'b0}}), .in9({32{1'b0}}),
    .in10({32{1'b0}}), .in11({32{1'b0}}), .in12({32{1'b0}}), .in13({32{1'b0}}), .in14({32{1'b0}}),
    .in15({32{1'b0}}), .out(Result_2), .sel(Switch));  // open: en

  // Other names for the same wires on the sheet: overflow = Signed_Overflow; S[3:0] = Switch

  // Notes on the sheet:
  //   INPUTS to your circuit
  //   DON'T CHANGE THE LOCATIONS OF THE INPUTS AND OUTPUTS!
  //   OUTPUTS from your circuit
endmodule

module Add_Subtract (
  input  [31:0] X,
  input  [31:0] Y,
  input  [3:0] selector,
  output [31:0] result,
  output OF
);

  wire adder_2_cout, and_1_out, and_2_out, bitselector_1_out, bitselector_2_out, bitselector_3_out,
       bitselector_4_out, comparator_1_eq, comparator_2_eq, comparator_3_eq, comparator_4_eq,
       multiplexer_2_out, not_3_out, or_1_out;
  wire [31:0] adder_1_out, multiplexer_1_out, not_1_out, not_2_out;

  assign not_1_out = ~Y;  // NOT_Gate not_1, 32 bits wide
  assign not_2_out = ~Y;  // NOT_Gate not_2, 32 bits wide
  Adder #(.width(32)) adder_1 (.a(32'h1), .b(not_1_out), .out(adder_1_out));  // open: cin, cout
  Multiplexer #(.select(4), .width(32)) multiplexer_1 (
    .in0(Y), .in1(Y), .in2(Y), .in3(Y), .in4(Y), .in5(Y), .in6(Y), .in7(adder_1_out), .in8(not_2_out),
    .in9(not_2_out), .in10(not_2_out), .in11(not_2_out), .in12(not_2_out), .in13(not_2_out),
    .in14(not_2_out), .in15(not_2_out), .out(multiplexer_1_out), .sel(selector));  // open: en
  BitSelector #(.width(4)) bitselector_1 (.in(selector), .out(bitselector_1_out), .sel(2'b00));
  Adder #(.width(32)) adder_2 (.a(X), .b(multiplexer_1_out), .out(result), .cout(adder_2_cout));  // open: cin
  Multiplexer #(.select(4)) multiplexer_2 (
    .in0(1'b0), .in1(1'b0), .in2(1'b0), .in3(1'b0), .in4(1'b0), .in5(bitselector_1_out), .in6(1'b0),
    .in7(bitselector_1_out), .in8(1'b0), .in9(1'b0), .in10(1'b0), .in11(1'b0), .in12(1'b0), .in13(1'b0),
    .in14(1'b0), .in15(1'b0), .out(multiplexer_2_out), .sel(selector));  // open: en
  BitSelector #(.width(32)) bitselector_2 (.in(X), .out(bitselector_2_out), .sel({5{1'b1}}));
  BitSelector #(.width(32)) bitselector_3 (.in(multiplexer_1_out), .out(bitselector_3_out), .sel({5{1'b1}}));
  Comparator #(.width(1), .mode("unsigned")) comparator_1 (
    .a(bitselector_2_out), .b(bitselector_3_out), .eq(comparator_1_eq));  // open: gt, lt
  BitSelector #(.width(32)) bitselector_4 (.in(result), .out(bitselector_4_out), .sel({5{1'b1}}));
  Comparator #(.width(1), .mode("unsigned")) comparator_2 (
    .a(bitselector_4_out), .b(bitselector_3_out), .eq(comparator_2_eq));  // open: gt, lt
  not not_3 (not_3_out, comparator_2_eq);
  Comparator #(.width(4), .mode("unsigned")) comparator_3 (
    .a(4'b0101), .b(selector), .eq(comparator_3_eq));  // open: gt, lt
  Comparator #(.width(4), .mode("unsigned")) comparator_4 (
    .a(4'b0111), .b(selector), .eq(comparator_4_eq));  // open: gt, lt
  and and_1 (and_1_out, not_3_out, comparator_1_eq);
  and and_2 (and_2_out, and_1_out, multiplexer_2_out);
  or or_1 (or_1_out, comparator_3_eq, comparator_4_eq);
  Multiplexer multiplexer_3 (.in0(adder_2_cout), .in1(and_2_out), .out(OF), .sel(or_1_out));  // open: en
endmodule

module Shift (
  input  [31:0] X,
  input  [31:0] Y,
  input  [3:0] in_3,
  output [31:0] out
);

  wire [4:0] bit_extender_1_out;
  wire [31:0] shifter_1_out, shifter_2_out, shifter_3_out;

  Bit_Extender #(.in_width(32), .out_width(5)) bit_extender_1 (.in(Y), .out(bit_extender_1_out));
  Shifter #(.width(32)) shifter_1 (.in(X), .\dist (bit_extender_1_out), .out(shifter_1_out));
  Shifter #(.width(32), .shift("lr")) shifter_2 (.in(X), .\dist (bit_extender_1_out), .out(shifter_2_out));
  Shifter #(.width(32), .shift("ar")) shifter_3 (.in(X), .\dist (bit_extender_1_out), .out(shifter_3_out));
  Multiplexer #(.select(4), .width(32)) multiplexer_1 (
    .in0(shifter_1_out), .in1(shifter_2_out), .in2(shifter_3_out), .out(out), .sel(in_3));  // open: in3, in4, in5, in6, in7, in8, in9, in10, in11, in12, in13, in14, in15, en
endmodule

module AND_OR_OUTER (
  input  [31:0] X,
  input  [31:0] Y,
  input  [3:0] select,
  output [31:0] result
);

  wire bit_extender_1_out;
  wire [31:0] and_1_out, or_1_out;

  assign or_1_out = X | Y;  // OR_Gate or_1, 32 bits wide
  assign and_1_out = X & Y;  // AND_Gate and_1, 32 bits wide
  Multiplexer #(.width(32)) multiplexer_1 (
    .in0(or_1_out), .in1(and_1_out), .out(result), .sel(bit_extender_1_out));  // open: en
  Bit_Extender #(.in_width(4), .out_width(1)) bit_extender_1 (.in(select), .out(bit_extender_1_out));
endmodule

module Mult (
  input  [31:0] X,
  input  [31:0] Y,
  output [31:0] result,
  output [31:0] result_2
);

  Multiplier #(.width(32)) multiplier_1 (.a(X), .b(Y), .out(result), .cout(result_2));  // open: cin
endmodule

module Div (
  input  [31:0] X,
  input  [31:0] Y,
  output [31:0] result,
  output [31:0] result_2
);

  Divider #(.width(32)) divider_1 (.a(X), .b(Y), .out(result), .rem(result_2));  // open: upper
endmodule

module slt (
  input  [31:0] X,
  input  [31:0] Y,
  input  [3:0] select,
  output [31:0] out_4
);

  wire bitselector_1_out, comparator_1_lt, comparator_2_lt;
  wire [31:0] bit_extender_1_out, bit_extender_2_out;

  Comparator #(.width(32), .mode("unsigned")) comparator_1 (.a(X), .b(Y), .lt(comparator_1_lt));  // open: gt, eq
  Comparator #(.width(32)) comparator_2 (.a(X), .b(Y), .lt(comparator_2_lt));  // open: gt, eq
  assign bit_extender_1_out = {{31{1'b0}}, comparator_1_lt};  // Bit_Extender bit_extender_1
  assign bit_extender_2_out = {{31{1'b0}}, comparator_2_lt};  // Bit_Extender bit_extender_2
  BitSelector #(.width(4)) bitselector_1 (.in(select), .out(bitselector_1_out), .sel(2'b01));
  Multiplexer #(.width(32)) multiplexer_1 (
    .in0(bit_extender_1_out), .in1(bit_extender_2_out), .out(out_4), .sel(bitselector_1_out));  // open: en
endmodule
