// Logisim project mem.circ as structural Verilog: 4 circuits, main circuit main
module main (
  input  [31:0] Addr,
  input  [31:0] Write_Data,
  input  [2:0] Op_Unit,
  input  Write_Enable,
  input  Clock,
  output [31:0] Read_Data
);

  wire [7:0] bit_extender_1_out, multiplexer_3_out;
  wire [15:0] bit_extender_2_out, multiplexer_4_out;
  wire [31:0] read_signed_byte_val, read_signed_half_val, read_unsigned_byte_val, read_unsigned_half_val,
       read_word_val, write_byte_val, write_data_t, write_half_val;

  Bit_Extender #(.in_width(32), .out_width(8)) bit_extender_1 (.in(Write_Data), .out(bit_extender_1_out));
  Bit_Extender #(.in_width(32)) bit_extender_2 (.in(Write_Data), .out(bit_extender_2_out));
  Multiplexer #(.width(32)) multiplexer_1 (
    .in0({bit_extender_2_out, read_word_val[15:0]}), .in1({read_word_val[31:16], bit_extender_2_out}),
    .out(write_half_val), .sel(Addr[1]));  // open: en
  Multiplexer #(.select(2), .width(32)) multiplexer_2 (
    .in0({bit_extender_1_out, read_word_val[15:8], read_word_val[23:16], read_word_val[31:24]}),
    .in1({read_word_val[7:0], bit_extender_1_out, read_word_val[23:16], read_word_val[31:24]}),
    .in2({read_word_val[7:0], read_word_val[15:8], bit_extender_1_out, read_word_val[31:24]}),
    .in3({read_word_val[7:0], read_word_val[15:8], read_word_val[23:16], bit_extender_1_out}),
    .out(write_byte_val), .sel(Addr[1:0]));  // open: en
  Multiplexer #(.select(2), .width(8)) multiplexer_3 (
    .in0(read_word_val[7:0]), .in1(read_word_val[15:8]), .in2(read_word_val[23:16]),
    .in3(read_word_val[31:24]), .out(multiplexer_3_out), .sel(Addr[1:0]));  // open: en
  Multiplexer #(.width(16)) multiplexer_4 (
    .in0(read_word_val[15:0]), .in1(read_word_val[31:16]), .out(multiplexer_4_out), .sel(Addr[1]));  // open: en
  assign read_unsigned_byte_val = {{24{1'b0}}, multiplexer_3_out};  // Bit_Extender bit_extender_3
  assign read_signed_byte_val = {{24{multiplexer_3_out[7]}}, multiplexer_3_out};  // Bit_Extender bit_extender_4
  assign read_unsigned_half_val = {{16{1'b0}}, multiplexer_4_out};  // Bit_Extender bit_extender_5
  assign read_signed_half_val = {{16{multiplexer_4_out[15]}}, multiplexer_4_out};  // Bit_Extender bit_extender_6
  Multiplexer #(.select(3), .width(32)) multiplexer_5 (
    .in0(write_byte_val), .in1(write_byte_val), .in2(write_half_val), .in3(write_half_val), .in4(Write_Data),
    .in5(Write_Data), .in6(Write_Data), .in7(Write_Data), .out(write_data_t), .sel(Op_Unit));  // open: en
  mem30 mem30_1 (
    .Addr(Addr[31:2]), .Write_Data(write_data_t), .Write_Enable(Write_Enable), .Clock(Clock),
    .Read_Data(read_word_val));
  Multiplexer #(.select(3), .width(32)) multiplexer_6 (
    .in0(read_unsigned_byte_val), .in1(read_signed_byte_val), .in2(read_unsigned_half_val),
    .in3(read_signed_half_val), .in4(read_word_val), .in5(read_word_val), .in6(read_word_val),
    .in7(read_word_val), .out(Read_Data), .sel(Op_Unit));  // open: en

  // Other names for the same wires on the sheet: byte_offset[1:0] = Addr[1:0]; half_offset = Addr[1];
  //   word_addr[29:0] = Addr[31:2]; clk = Clock; data_out[31:0] = Read_Data; write_en = Write_Enable;
  //   write_word_val[31:0] = Write_Data

  // Notes on the sheet:
  //   DO NOT MODIFY
endmodule

module mem26 (
  input  [25:0] Addr,
  input  [31:0] Write_Data,
  input  Write_Enable,
  input  Clock,
  output [31:0] Read_Data
);

  wire write_en_0, write_en_1, write_en_2, write_en_3;
  wire [31:0] word_data_0, word_data_1, word_data_2, word_data_3;

  RAM #(.addrWidth(24), .dataWidth(32), .bus("separate")) ram_1 (
    .addr(Addr[23:0]), .din(Write_Data), .data(word_data_0), .str(write_en_0), .clk(Clock));  // open: sel, ld, clr
  RAM #(.addrWidth(24), .dataWidth(32), .bus("separate")) ram_2 (
    .addr(Addr[23:0]), .din(Write_Data), .data(word_data_1), .str(write_en_1), .clk(Clock));  // open: sel, ld, clr
  Multiplexer #(.select(2), .width(32)) multiplexer_1 (
    .in0(word_data_0), .in1(word_data_1), .in2(word_data_2), .in3(word_data_3), .out(Read_Data),
    .sel(Addr[25:24]));  // open: en
  Demultiplexer #(.select(2), .enable("false")) demultiplexer_1 (
    .out0(write_en_0), .out1(write_en_1), .out2(write_en_2), .out3(write_en_3), .in(Write_Enable),
    .sel(Addr[25:24]));
  RAM #(.addrWidth(24), .dataWidth(32), .bus("separate")) ram_3 (
    .addr(Addr[23:0]), .din(Write_Data), .data(word_data_2), .str(write_en_2), .clk(Clock));  // open: sel, ld, clr
  RAM #(.addrWidth(24), .dataWidth(32), .bus("separate")) ram_4 (
    .addr(Addr[23:0]), .din(Write_Data), .data(word_data_3), .str(write_en_3), .clk(Clock));  // open: sel, ld, clr

  // Other names for the same wires on the sheet: addr_t[23:0] = Addr[23:0]; addr_top[1:0] = Addr[25:24]; clk = Clock;
  //   data_in[31:0] = Write_Data; write_en = Write_Enable

  // Notes on the sheet:
  //   DO NOT MODIFY
endmodule

module mem28 (
  input  [27:0] Addr,
  input  [31:0] Write_Data,
  input  Write_Enable,
  input  Clock,
  output [31:0] Read_Data
);

  wire write_en_0, write_en_1, write_en_2, write_en_3;
  wire [31:0] word_data_0, word_data_1, word_data_2, word_data_3;

  mem26 mem26_1 (
    .Addr(Addr[25:0]), .Write_Data(Write_Data), .Write_Enable(write_en_0), .Clock(Clock),
    .Read_Data(word_data_0));
  mem26 mem26_2 (
    .Addr(Addr[25:0]), .Write_Data(Write_Data), .Write_Enable(write_en_1), .Clock(Clock),
    .Read_Data(word_data_1));
  Multiplexer #(.select(2), .width(32)) multiplexer_1 (
    .in0(word_data_0), .in1(word_data_1), .in2(word_data_2), .in3(word_data_3), .out(Read_Data),
    .sel(Addr[27:26]));  // open: en
  Demultiplexer #(.select(2), .enable("false")) demultiplexer_1 (
    .out0(write_en_0), .out1(write_en_1), .out2(write_en_2), .out3(write_en_3), .in(Write_Enable),
    .sel(Addr[27:26]));
  mem26 mem26_3 (
    .Addr(Addr[25:0]), .Write_Data(Write_Data), .Write_Enable(write_en_2), .Clock(Clock),
    .Read_Data(word_data_2));
  mem26 mem26_4 (
    .Addr(Addr[25:0]), .Write_Data(Write_Data), .Write_Enable(write_en_3), .Clock(Clock),
    .Read_Data(word_data_3));

  // Other names for the same wires on the sheet: addr_t[25:0] = Addr[25:0]; addr_top[1:0] = Addr[27:26]; clk = Clock;
  //   data_in[31:0] = Write_Data; write_en = Write_Enable

  // Notes on the sheet:
  //   DO NOT MODIFY
endmodule

module mem30 (
  input  [29:0] Addr,
  input  [31:0] Write_Data,
  input  Write_Enable,
  input  Clock,
  output [31:0] Read_Data
);

  wire write_en_0, write_en_1, write_en_2, write_en_3;
  wire [31:0] word_data_0, word_data_1, word_data_2, word_data_3;

  mem28 mem28_1 (
    .Addr(Addr[27:0]), .Write_Data(Write_Data), .Write_Enable(write_en_0), .Clock(Clock),
    .Read_Data(word_data_0));
  mem28 mem28_2 (
    .Addr(Addr[27:0]), .Write_Data(Write_Data), .Write_Enable(write_en_1), .Clock(Clock),
    .Read_Data(word_data_1));
  Multiplexer #(.select(2), .width(32)) multiplexer_1 (
    .in0(word_data_0), .in1(word_data_1), .in2(word_data_2), .in3(word_data_3), .out(Read_Data),
    .sel(Addr[29:28]));  // open: en
  Demultiplexer #(.select(2), .enable("false")) demultiplexer_1 (
    .out0(write_en_0), .out1(write_en_1), .out2(write_en_2), .out3(write_en_3), .in(Write_Enable),
    .sel(Addr[29:28]));
  mem28 mem28_3 (
    .Addr(Addr[27:0]), .Write_Data(Write_Data), .Write_Enable(write_en_2), .Clock(Clock),
    .Read_Data(word_data_2));
  mem28 mem28_4 (
    .Addr(Addr[27:0]), .Write_Data(Write_Data), .Write_Enable(write_en_3), .Clock(Clock),
    .Read_Data(word_data_3));

  // Other names for the same wires on the sheet: addr_t[27:0] = Addr[27:0]; addr_top[1:0] = Addr[29:28]; clk = Clock;
  //   data_in[31:0] = Write_Data; write_en = Write_Enable

  // Notes on the sheet:
  //   DO NOT MODIFY
endmodule
