// Logisim project regfile.circ as structural Verilog: 2 circuits, main circuit main
module main (
  input  [4:0] Read_Register_1,
  input  [4:0] Read_Register_2,
  input  [4:0] Write_Register,
  input  [31:0] Write_Data,
  input  Write_Enable,
  input  Clock,
  input  in_7,
  output [31:0] s0_Value,
  output [31:0] s1_Value,
  output [31:0] s2_Value,
  output [31:0] ra_Value,
  output [31:0] Read_Data_1,
  output [31:0] Read_Data_2
);

  wire WR____0, WR____a0, WR____a1, WR____a2, WR____a3, WR____at, WR____fp, WR____gp, WR____k0, WR____k1,
       WR____ra, WR____s0, WR____s1, WR____s2, WR____s3, WR____s4, WR____s5, WR____s6, WR____s7, WR____sp,
       WR____t0, WR____t1, WR____t2, WR____t3, WR____t4, WR____t5, WR____t6, WR____t7, WR____t8, WR____t9,
       WR____v0, WR____v1;
  wire [31:0] RR1____0, RR1____a0, RR1____a1, RR1____a2, RR1____a3, RR1____at, RR1____at_t, RR1____fp,
       RR1____gp, RR1____k0, RR1____k1, RR1____s3, RR1____s4, RR1____s5, RR1____s6, RR1____s7, RR1____sp,
       RR1____t0, RR1____t1, RR1____t2, RR1____t3, RR1____t4, RR1____t5, RR1____t6, RR1____t7, RR1____t8,
       RR1____t9, RR1____v0, RR1____v0_t, RR1____v1, wr_selector_1_write_output, wr_selector_2_write_output,
       wr_selector_3_write_output, wr_selector_4_write_output, wr_selector_5_write_output,
       wr_selector_6_write_output, wr_selector_7_write_output, wr_selector_8_write_output,
       wr_selector_9_write_output, wr_selector_10_write_output, wr_selector_11_write_output,
       wr_selector_12_write_output, wr_selector_13_write_output, wr_selector_14_write_output,
       wr_selector_15_write_output, wr_selector_16_write_output, wr_selector_17_write_output,
       wr_selector_18_write_output, wr_selector_19_write_output, wr_selector_20_write_output,
       wr_selector_21_write_output, wr_selector_22_write_output, wr_selector_23_write_output,
       wr_selector_24_write_output, wr_selector_25_write_output, wr_selector_26_write_output,
       wr_selector_27_write_output, wr_selector_28_write_output, wr_selector_29_write_output,
       wr_selector_30_write_output, wr_selector_31_write_output;

  Demultiplexer #(.select(5)) demultiplexer_1 (
    .out0(WR____0), .out1(WR____at), .out2(WR____v0), .out3(WR____v1), .out4(WR____a0), .out5(WR____a1),
    .out6(WR____a2), .out7(WR____a3), .out8(WR____t0), .out9(WR____t1), .out10(WR____t2), .out11(WR____t3),
    .out12(WR____t4), .out13(WR____t5), .out14(WR____t6), .out15(WR____t7), .out16(WR____s0),
    .out17(WR____s1), .out18(WR____s2), .out19(WR____s3), .out20(WR____s4), .out21(WR____s5),
    .out22(WR____s6), .out23(WR____s7), .out24(WR____t8), .out25(WR____t9), .out26(WR____k0),
    .out27(WR____k1), .out28(WR____gp), .out29(WR____sp), .out30(WR____fp), .out31(WR____ra), .in(in_7),
    .sel(Write_Register), .en(Write_Enable));
  Register #(.width(32)) Reg__0 (.Q(RR1____0));  // open: D, en, clk, clr
  Register #(.width(32)) Reg_a0 (.D(wr_selector_1_write_output), .Q(RR1____a0), .clk(Clock));  // open: en, clr
  WR_Selector wr_selector_1 (.Write_Input(Write_Data), .Write_Output(wr_selector_1_write_output), .WR(WR____a0));
  Register #(.width(32)) Reg_t0 (.D(wr_selector_2_write_output), .Q(RR1____t0), .clk(Clock));  // open: en, clr
  WR_Selector wr_selector_2 (.Write_Input(Write_Data), .Write_Output(wr_selector_2_write_output), .WR(WR____t0));
  WR_Selector wr_selector_3 (.Write_Input(Write_Data), .Write_Output(wr_selector_3_write_output), .WR(WR____t4));
  Register #(.width(32)) Reg_t4 (.D(wr_selector_3_write_output), .Q(RR1____t4), .clk(Clock));  // open: en, clr
  Register #(.width(32)) Reg_s0 (.D(wr_selector_4_write_output), .Q(s0_Value), .clk(Clock));  // open: en, clr
  WR_Selector wr_selector_4 (.Write_Input(Write_Data), .Write_Output(wr_selector_4_write_output), .WR(WR____s0));
  WR_Selector wr_selector_5 (.Write_Input(Write_Data), .Write_Output(wr_selector_5_write_output), .WR(WR____s4));
  Register #(.width(32)) Reg_s4 (.D(wr_selector_5_write_output), .Q(RR1____s4), .clk(Clock));  // open: en, clr
  WR_Selector wr_selector_6 (.Write_Input(Write_Data), .Write_Output(wr_selector_6_write_output), .WR(WR____t8));
  Register #(.width(32)) Reg_t8 (.D(wr_selector_6_write_output), .Q(RR1____t8), .clk(Clock));  // open: en, clr
  WR_Selector wr_selector_7 (.Write_Input(Write_Data), .Write_Output(wr_selector_7_write_output), .WR(WR____gp));
  Register #(.width(32)) Reg_gp (.D(wr_selector_7_write_output), .Q(RR1____gp), .clk(Clock));  // open: en, clr
  Register #(.width(32)) Reg_at (.D(wr_selector_8_write_output), .Q(RR1____at_t), .clk(Clock));  // open: en, clr
  WR_Selector wr_selector_8 (.Write_Input(Write_Data), .Write_Output(wr_selector_8_write_output), .WR(WR____at));
  WR_Selector wr_selector_9 (.Write_Input(Write_Data), .Write_Output(wr_selector_9_write_output), .WR(WR____a1));
  Register #(.width(32)) Reg_a1 (.D(wr_selector_9_write_output), .Q(RR1____a1), .clk(Clock));  // open: en, clr
  WR_Selector wr_selector_10 (.Write_Input(Write_Data), .Write_Output(wr_selector_10_write_output), .WR(WR____t1));
  Register #(.width(32)) Reg_t1 (.D(wr_selector_10_write_output), .Q(RR1____t1), .clk(Clock));  // open: en, clr
  Register #(.width(32)) Reg_t5 (.D(wr_selector_11_write_output), .Q(RR1____t5), .clk(Clock));  // open: en, clr
  WR_Selector wr_selector_11 (.Write_Input(Write_Data), .Write_Output(wr_selector_11_write_output), .WR(WR____t5));
  Register #(.width(32)) Reg_s1 (.D(wr_selector_12_write_output), .Q(s1_Value), .clk(Clock));  // open: en, clr
  WR_Selector wr_selector_12 (.Write_Input(Write_Data), .Write_Output(wr_selector_12_write_output), .WR(WR____s1));
  WR_Selector wr_selector_13 (.Write_Input(Write_Data), .Write_Output(wr_selector_13_write_output), .WR(WR____s5));
  Register #(.width(32)) Reg_s5 (.D(wr_selector_13_write_output), .Q(RR1____s5), .clk(Clock));  // open: en, clr
  Register #(.width(32)) Reg_t9 (.D(wr_selector_14_write_output), .Q(RR1____t9), .clk(Clock));  // open: en, clr
  WR_Selector wr_selector_14 (.Write_Input(Write_Data), .Write_Output(wr_selector_14_write_output), .WR(WR____t9));
  Register #(.width(32)) Reg_sp (.D(wr_selector_15_write_output), .Q(RR1____sp), .clk(Clock));  // open: en, clr
  WR_Selector wr_selector_15 (.Write_Input(Write_Data), .Write_Output(wr_selector_15_write_output), .WR(WR____sp));
  WR_Selector wr_selector_16 (.Write_Input(Write_Data), .Write_Output(wr_selector_16_write_output), .WR(WR____v0));
  WR_Selector wr_selector_17 (.Write_Input(Write_Data), .Write_Output(wr_selector_17_write_output), .WR(WR____a2));
  WR_Selector wr_selector_18 (.Write_Input(Write_Data), .Write_Output(wr_selector_18_write_output), .WR(WR____t2));
  WR_Selector wr_selector_19 (.Write_Input(Write_Data), .Write_Output(wr_selector_19_write_output), .WR(WR____t6));
  WR_Selector wr_selector_20 (.Write_Input(Write_Data), .Write_Output(wr_selector_20_write_output), .WR(WR____s2));
  WR_Selector wr_selector_21 (.Write_Input(Write_Data), .Write_Output(wr_selector_21_write_output), .WR(WR____s6));
  WR_Selector wr_selector_22 (.Write_Input(Write_Data), .Write_Output(wr_selector_22_write_output), .WR(WR____k0));
  WR_Selector wr_selector_23 (.Write_Input(Write_Data), .Write_Output(wr_selector_23_write_output), .WR(WR____fp));
  Register #(.width(32)) Reg_v0 (.D(wr_selector_16_write_output), .Q(RR1____v0_t), .clk(Clock));  // open: en, clr
  Register #(.width(32)) Reg_a2 (.D(wr_selector_17_write_output), .Q(RR1____a2), .clk(Clock));  // open: en, clr
  Register #(.width(32)) Reg_t2 (.D(wr_selector_18_write_output), .Q(RR1____t2), .clk(Clock));  // open: en, clr
  Register #(.width(32)) Reg_t6 (.D(wr_selector_19_write_output), .Q(RR1____t6), .clk(Clock));  // open: en, clr
  Register #(.width(32)) Reg_s2 (.D(wr_selector_20_write_output), .Q(s2_Value), .clk(Clock));  // open: en, clr
  Register #(.width(32)) Reg_s6 (.D(wr_selector_21_write_output), .Q(RR1____s6), .clk(Clock));  // open: en, clr
  Register #(.width(32)) Reg_k0 (.D(wr_selector_22_write_output), .Q(RR1____k0), .clk(Clock));  // open: en, clr
  Register #(.width(32)) Reg_fp (.D(wr_selector_23_write_output), .Q(RR1____fp), .clk(Clock));  // open: en, clr
  WR_Selector wr_selector_24 (.Write_Input(Write_Data), .Write_Output(wr_selector_24_write_output), .WR(WR____v1));
  WR_Selector wr_selector_25 (.Write_Input(Write_Data), .Write_Output(wr_selector_25_write_output), .WR(WR____a3));
  WR_Selector wr_selector_26 (.Write_Input(Write_Data), .Write_Output(wr_selector_26_write_output), .WR(WR____t3));
  WR_Selector wr_selector_27 (.Write_Input(Write_Data), .Write_Output(wr_selector_27_write_output), .WR(WR____t7));
  WR_Selector wr_selector_28 (.Write_Input(Write_Data), .Write_Output(wr_selector_28_write_output), .WR(WR____s3));
  WR_Selector wr_selector_29 (.Write_Input(Write_Data), .Write_Output(wr_selector_29_write_output), .WR(WR____s7));
  WR_Selector wr_selector_30 (.Write_Input(Write_Data), .Write_Output(wr_selector_30_write_output), .WR(WR____k1));
  WR_Selector wr_selector_31 (.Write_Input(Write_Data), .Write_Output(wr_selector_31_write_output), .WR(WR____ra));
  Register #(.width(32)) Reg_v1 (.D(wr_selector_24_write_output), .Q(RR1____v1), .clk(Clock));  // open: en, clr
  Register #(.width(32)) Reg_a3 (.D(wr_selector_25_write_output), .Q(RR1____a3), .clk(Clock));  // open: en, clr
  Register #(.width(32)) Reg_t3 (.D(wr_selector_26_write_output), .Q(RR1____t3), .clk(Clock));  // open: en, clr
  Register #(.width(32)) Reg_t7 (.D(wr_selector_27_write_output), .Q(RR1____t7), .clk(Clock));  // open: en, clr
  Register #(.width(32)) Reg_s3 (.D(wr_selector_28_write_output), .Q(RR1____s3), .clk(Clock));  // open: en, clr
  Register #(.width(32)) Reg_s7 (.D(wr_selector_29_write_output), .Q(RR1____s7), .clk(Clock));  // open: en, clr
  Register #(.width(32)) Reg_k1 (.D(wr_selector_30_write_output), .Q(RR1____k1), .clk(Clock));  // open: en, clr
  Register #(.width(32)) Reg_ra (.D(wr_selector_31_write_output), .Q(ra_Value), .clk(Clock));  // open: en, clr
  Multiplexer #(.select(5), .width(32), .enable("false")) multiplexer_1 (
    .in0(RR1____0), .in1(RR1____at), .in2(RR1____v0), .in3(RR1____v1), .in4(RR1____a0), .in5(RR1____a1),
    .in6(RR1____a2), .in7(RR1____a3), .in8(RR1____t0), .in9(RR1____t1), .in10(RR1____t2), .in11(RR1____t3),
    .in12(RR1____t4), .in13(RR1____t5), .in14(RR1____t6), .in15(RR1____t7), .in16(s0_Value), .in17(s1_Value),
    .in18(s2_Value), .in19(RR1____s3), .in20(RR1____s4), .in21(RR1____s5), .in22(RR1____s6),
    .in23(RR1____s7), .in24(RR1____t8), .in25(RR1____t9), .in26(RR1____k0), .in27(RR1____k1),
    .in28(RR1____gp), .in29(RR1____sp), .in30(RR1____fp), .in31(ra_Value), .out(Read_Data_1),
    .sel(Read_Register_1));
  Multiplexer #(.select(5), .width(32), .enable("false")) multiplexer_2 (
    .in0(RR1____0), .in1(RR1____at_t), .in2(RR1____v0_t), .in3(RR1____v1), .in4(RR1____a0), .in5(RR1____a1),
    .in6(RR1____a2), .in7(RR1____a3), .in8(RR1____t0), .in9(RR1____t1), .in10(RR1____t2), .in11(RR1____t3),
    .in12(RR1____t4), .in13(RR1____t5), .in14(RR1____t6), .in15(RR1____t7), .in16(s0_Value), .in17(s1_Value),
    .in18(s2_Value), .in19(RR1____s3), .in20(RR1____s4), .in21(RR1____s5), .in22(RR1____s6),
    .in23(RR1____s7), .in24(RR1____t8), .in25(RR1____t9), .in26(RR1____k0), .in27(RR1____k1),
    .in28(RR1____gp), .in29(RR1____sp), .in30(RR1____fp), .in31(ra_Value), .out(Read_Data_2),
    .sel(Read_Register_2));

  // Other names for the same wires on the sheet: clk = Clock; read_data1[31:0] = Read_Data_1;
  //   read_data2[31:0] = Read_Data_2; read_reg1[4:0] = Read_Register_1; read_reg2[4:0] = Read_Register_2;
  //   RR2____0[31:0] = RR1____0; RR2____a0[31:0] = RR1____a0; RR2____a1[31:0] = RR1____a1;
  //   RR2____a2[31:0] = RR1____a2; RR2____a3[31:0] = RR1____a3; RR2____at[31:0] = RR1____at_t;
  //   RR2____fp[31:0] = RR1____fp; RR2____gp[31:0] = RR1____gp; RR2____k0[31:0] = RR1____k0;
  //   RR2____k1[31:0] = RR1____k1; RR1____ra[31:0] = ra_Value; RR2____ra[31:0] = ra_Value; RR1____s0[31:0] = s0_Value;
  //   RR2____s0[31:0] = s0_Value; RR1____s1[31:0] = s1_Value; RR2____s1[31:0] = s1_Value; RR1____s2[31:0] = s2_Value;
  //   RR2____s2[31:0] = s2_Value; RR2____s3[31:0] = RR1____s3; RR2____s4[31:0] = RR1____s4;
  //   RR2____s5[31:0] = RR1____s5; RR2____s6[31:0] = RR1____s6; RR2____s7[31:0] = RR1____s7;
  //   RR2____sp[31:0] = RR1____sp; RR2____t0[31:0] = RR1____t0; RR2____t1[31:0] = RR1____t1;
  //   RR2____t2[31:0] = RR1____t2; RR2____t3[31:0] = RR1____t3; RR2____t4[31:0] = RR1____t4;
  //   RR2____t5[31:0] = RR1____t5; RR2____t6[31:0] = RR1____t6; RR2____t7[31:0] = RR1____t7;
  //   RR2____t8[31:0] = RR1____t8; RR2____t9[31:0] = RR1____t9; RR2____v0[31:0] = RR1____v0_t;
  //   RR2____v1[31:0] = RR1____v1; write_en = Write_Enable; write_reg[4:0] = Write_Register

  // Notes on the sheet:
  //   INPUTS to your circuit
  //   DON'T CHANGE THE LOCATIONS OF THE INPUTS AND OUTPUTS!
  //   These are DEBUG/TEST outputs from your circuit.
  //   OUTPUTS from your circuit
endmodule

// WR
module WR_Selector (
  input  [31:0] Write_Input,
  input  WR,
  output [31:0] Write_Output
);

  Multiplexer #(.width(32), .enable("false")) multiplexer_1 (
    .in1(Write_Input), .out(Write_Output), .sel(WR));  // open: in0
endmodule
